// Logisim project CPU.circ as structural Verilog: 2 circuits, main circuit main
module main (
);

  wire clock_1_out, Decode_Clock_betw, execute_1_cnd, Execute_Clock_betw, fetch_1_halt, Fetch_Clock_betw,
       Memory_Clock_betw, PC_Update_Clock_betw, WB_Clock_betw;
  wire [3:0] fetch_1_icode, fetch_1_ifun, fetch_1_ra, fetch_1_rb;
  wire [11:0] counter_1_q, fetch_1_val_p, multiplexer_1_out, newpc_1_new_pc;
  wire [63:0] bitselector_1_out, decode_1_vala, decode_1_valb, execute_1_vale, fetch_1_valc, memory_1_valm;

  Clock clock_1 (.out(clock_1_out));
  Counter #(.max('h19), .width(12)) counter_1 (
    .clk(clock_1_out), .Q(counter_1_q));  // open: clr, load, up, count, D, carry
  LED led_1 (.in(fetch_1_halt));
  newPC newpc_1 (
    .valP(bitselector_1_out), .valC(fetch_1_valc), .Cnd(execute_1_cnd), .valM(memory_1_valm),
    .icode(fetch_1_icode), .clk(clock_1_out), .Enable(PC_Update_Clock_betw), .new_PC(newpc_1_new_pc));
  Memory memory_1 (
    .icode(fetch_1_icode), .ValP(bitselector_1_out), .ValE(execute_1_vale), .ValA(decode_1_vala),
    .clk(clock_1_out), .Enable(Memory_Clock_betw), .ValM(memory_1_valm));
  Execute execute_1 (
    .icode(fetch_1_icode), .ifun(fetch_1_ifun), .valC(fetch_1_valc), .valA(decode_1_vala),
    .valB(decode_1_valb), .Clk(clock_1_out), .Enable(Execute_Clock_betw), .Cnd(execute_1_cnd),
    .valE(execute_1_vale));
  Decode decode_1 (
    .icode(fetch_1_icode), .ifun(fetch_1_ifun), .ValM(memory_1_valm), .ValE(execute_1_vale), .rA(fetch_1_ra),
    .rB(fetch_1_rb), .Read_Enable(Decode_Clock_betw), .Write_Enable(WB_Clock_betw), .Clk(clock_1_out),
    .ValA(decode_1_vala), .ValB(decode_1_valb));
  Fetch fetch_1 (
    .PC_in(newpc_1_new_pc), .Clk(clock_1_out), .Enable(Fetch_Clock_betw), .Halt(fetch_1_halt),
    .icode(fetch_1_icode), .ifun(fetch_1_ifun), .rA(fetch_1_ra), .rB(fetch_1_rb), .ValC(fetch_1_valc),
    .Val_P(fetch_1_val_p));
  Multiplexer #(.width(12)) multiplexer_1 (
    .in0(counter_1_q), .in1({12{1'b1}}), .out(multiplexer_1_out), .sel(fetch_1_halt));
  BitSelector #(.group(64), .width(12)) bitselector_1 (.in(fetch_1_val_p), .out(bitselector_1_out), .sel(1'b0));
  Between PC_Update_Clock (.less(12'h19), .val(multiplexer_1_out), .greater(12'h18), .betw(PC_Update_Clock_betw));
  Between WB_Clock (.less(12'h18), .val(multiplexer_1_out), .greater(12'h16), .betw(WB_Clock_betw));
  Between Memory_Clock (.less(12'h16), .val(multiplexer_1_out), .greater(12'hd), .betw(Memory_Clock_betw));
  Between Execute_Clock (.less(12'hd), .val(multiplexer_1_out), .greater(12'hc), .betw(Execute_Clock_betw));
  Between Decode_Clock (.less(12'hc), .val(multiplexer_1_out), .greater(12'ha), .betw(Decode_Clock_betw));
  Between Fetch_Clock (.less(12'ha), .val(multiplexer_1_out), .greater({12{1'b0}}), .betw(Fetch_Clock_betw));
endmodule

module Between (
  input  [11:0] less,
  input  [11:0] val,
  input  [11:0] greater,
  output betw
);

  wire comparator_1_gt, comparator_2_eq, comparator_2_gt, or_1_out;

  Comparator #(.width(12)) comparator_1 (.a(less), .b(val), .gt(comparator_1_gt));  // open: eq, lt
  Comparator #(.width(12)) comparator_2 (.a(val), .b(greater), .gt(comparator_2_gt), .eq(comparator_2_eq));  // open: lt
  or or_1 (or_1_out, comparator_2_gt, comparator_2_eq);
  and and_1 (betw, comparator_1_gt, or_1_out);
endmodule
