// Logisim project Decode_Stage.circ as structural Verilog: 2 circuits, main circuit Register_File
module Register_File (
  input  [3:0] srcA,
  input  [3:0] srcB,
  input  [3:0] dstE,
  input  [63:0] ValE,
  input  [3:0] dstM,
  input  [63:0] ValM,
  input  Clk,
  input  Read_Enable,
  input  Write_Enable,
  output [63:0] ValA,
  output [63:0] ValB
);

  wire demultiplexer_1_out0, demultiplexer_1_out1, demultiplexer_1_out2, demultiplexer_1_out3,
       demultiplexer_1_out4, demultiplexer_1_out5, demultiplexer_1_out6, demultiplexer_1_out7,
       demultiplexer_1_out8, demultiplexer_1_out9, demultiplexer_1_out10, demultiplexer_1_out11,
       demultiplexer_1_out12, demultiplexer_1_out13, demultiplexer_1_out14, demultiplexer_2_out0,
       demultiplexer_2_out1, demultiplexer_2_out2, demultiplexer_2_out3, demultiplexer_2_out4,
       demultiplexer_2_out5, demultiplexer_2_out6, demultiplexer_2_out7, demultiplexer_2_out8,
       demultiplexer_2_out9, demultiplexer_2_out10, demultiplexer_2_out11, demultiplexer_2_out12,
       demultiplexer_2_out13, demultiplexer_2_out14, or_1_out, or_2_out, or_3_out, or_4_out, or_5_out,
       or_6_out, or_7_out, or_8_out, or_9_out, or_10_out, or_11_out, or_12_out, or_13_out, or_14_out,
       or_15_out;
  wire [63:0] controlled_buffer_1_out, controlled_buffer_3_out, controlled_buffer_5_out,
       controlled_buffer_7_out, controlled_buffer_9_out, controlled_buffer_11_out, controlled_buffer_13_out,
       controlled_buffer_15_out, controlled_buffer_17_out, controlled_buffer_19_out,
       controlled_buffer_21_out, controlled_buffer_23_out, controlled_buffer_25_out,
       controlled_buffer_27_out, controlled_buffer_29_out, multiplexer_1_out, multiplexer_2_out,
       register_1_q, register_2_q, register_3_q, register_4_q, register_5_q, register_6_q, register_7_q,
       register_8_q, register_9_q, register_10_q, register_11_q, register_12_q, register_13_q, register_14_q,
       register_15_q;

  Demultiplexer #(.select(4)) demultiplexer_1 (
    .out0(demultiplexer_1_out0), .out1(demultiplexer_1_out1), .out2(demultiplexer_1_out2),
    .out3(demultiplexer_1_out3), .out4(demultiplexer_1_out4), .out5(demultiplexer_1_out5),
    .out6(demultiplexer_1_out6), .out7(demultiplexer_1_out7), .out8(demultiplexer_1_out8),
    .out9(demultiplexer_1_out9), .out10(demultiplexer_1_out10), .out11(demultiplexer_1_out11),
    .out12(demultiplexer_1_out12), .out13(demultiplexer_1_out13), .out14(demultiplexer_1_out14),
    .in(Write_Enable), .sel(dstE));  // open: out15
  Demultiplexer #(.select(4)) demultiplexer_2 (
    .out0(demultiplexer_2_out0), .out1(demultiplexer_2_out1), .out2(demultiplexer_2_out2),
    .out3(demultiplexer_2_out3), .out4(demultiplexer_2_out4), .out5(demultiplexer_2_out5),
    .out6(demultiplexer_2_out6), .out7(demultiplexer_2_out7), .out8(demultiplexer_2_out8),
    .out9(demultiplexer_2_out9), .out10(demultiplexer_2_out10), .out11(demultiplexer_2_out11),
    .out12(demultiplexer_2_out12), .out13(demultiplexer_2_out13), .out14(demultiplexer_2_out14),
    .in(Write_Enable), .sel(dstM));  // open: out15
  assign controlled_buffer_1_out = demultiplexer_1_out0 ? ValE : 64'bz;  // Controlled_Buffer controlled_buffer_1
  or or_1 (or_1_out, demultiplexer_1_out0, demultiplexer_2_out0);
  assign controlled_buffer_1_out = demultiplexer_2_out0 ? ValM : 64'bz;  // Controlled_Buffer controlled_buffer_2
  assign controlled_buffer_3_out = demultiplexer_1_out1 ? ValE : 64'bz;  // Controlled_Buffer controlled_buffer_3
  or or_2 (or_2_out, demultiplexer_1_out1, demultiplexer_2_out1);
  assign controlled_buffer_3_out = demultiplexer_2_out1 ? ValM : 64'bz;  // Controlled_Buffer controlled_buffer_4
  assign controlled_buffer_5_out = demultiplexer_1_out2 ? ValE : 64'bz;  // Controlled_Buffer controlled_buffer_5
  or or_3 (or_3_out, demultiplexer_1_out2, demultiplexer_2_out2);
  assign controlled_buffer_5_out = demultiplexer_2_out2 ? ValM : 64'bz;  // Controlled_Buffer controlled_buffer_6
  assign controlled_buffer_7_out = demultiplexer_1_out3 ? ValE : 64'bz;  // Controlled_Buffer controlled_buffer_7
  or or_4 (or_4_out, demultiplexer_1_out3, demultiplexer_2_out3);
  assign controlled_buffer_7_out = demultiplexer_2_out3 ? ValM : 64'bz;  // Controlled_Buffer controlled_buffer_8
  assign controlled_buffer_9_out = demultiplexer_1_out4 ? ValE : 64'bz;  // Controlled_Buffer controlled_buffer_9
  or or_5 (or_5_out, demultiplexer_1_out4, demultiplexer_2_out4);
  assign controlled_buffer_9_out = demultiplexer_2_out4 ? ValM : 64'bz;  // Controlled_Buffer controlled_buffer_10
  assign controlled_buffer_11_out = demultiplexer_1_out5 ? ValE : 64'bz;  // Controlled_Buffer controlled_buffer_11
  or or_6 (or_6_out, demultiplexer_1_out5, demultiplexer_2_out5);
  assign controlled_buffer_11_out = demultiplexer_2_out5 ? ValM : 64'bz;  // Controlled_Buffer controlled_buffer_12
  assign controlled_buffer_13_out = demultiplexer_1_out6 ? ValE : 64'bz;  // Controlled_Buffer controlled_buffer_13
  or or_7 (or_7_out, demultiplexer_1_out6, demultiplexer_2_out6);
  assign controlled_buffer_13_out = demultiplexer_2_out6 ? ValM : 64'bz;  // Controlled_Buffer controlled_buffer_14
  assign controlled_buffer_15_out = demultiplexer_1_out7 ? ValE : 64'bz;  // Controlled_Buffer controlled_buffer_15
  or or_8 (or_8_out, demultiplexer_1_out7, demultiplexer_2_out7);
  assign controlled_buffer_15_out = demultiplexer_2_out7 ? ValM : 64'bz;  // Controlled_Buffer controlled_buffer_16
  assign controlled_buffer_17_out = demultiplexer_1_out8 ? ValE : 64'bz;  // Controlled_Buffer controlled_buffer_17
  or or_9 (or_9_out, demultiplexer_1_out8, demultiplexer_2_out8);
  assign controlled_buffer_17_out = demultiplexer_2_out8 ? ValM : 64'bz;  // Controlled_Buffer controlled_buffer_18
  assign controlled_buffer_19_out = demultiplexer_1_out9 ? ValE : 64'bz;  // Controlled_Buffer controlled_buffer_19
  or or_10 (or_10_out, demultiplexer_1_out9, demultiplexer_2_out9);
  assign controlled_buffer_19_out = demultiplexer_2_out9 ? ValM : 64'bz;  // Controlled_Buffer controlled_buffer_20
  assign controlled_buffer_21_out = demultiplexer_1_out10 ? ValE : 64'bz;  // Controlled_Buffer controlled_buffer_21
  or or_11 (or_11_out, demultiplexer_1_out10, demultiplexer_2_out10);
  assign controlled_buffer_21_out = demultiplexer_2_out10 ? ValM : 64'bz;  // Controlled_Buffer controlled_buffer_22
  assign controlled_buffer_23_out = demultiplexer_1_out11 ? ValE : 64'bz;  // Controlled_Buffer controlled_buffer_23
  or or_12 (or_12_out, demultiplexer_1_out11, demultiplexer_2_out11);
  assign controlled_buffer_23_out = demultiplexer_2_out11 ? ValM : 64'bz;  // Controlled_Buffer controlled_buffer_24
  assign controlled_buffer_25_out = demultiplexer_1_out12 ? ValE : 64'bz;  // Controlled_Buffer controlled_buffer_25
  or or_13 (or_13_out, demultiplexer_1_out12, demultiplexer_2_out12);
  assign controlled_buffer_25_out = demultiplexer_2_out12 ? ValM : 64'bz;  // Controlled_Buffer controlled_buffer_26
  assign controlled_buffer_27_out = demultiplexer_1_out13 ? ValE : 64'bz;  // Controlled_Buffer controlled_buffer_27
  or or_14 (or_14_out, demultiplexer_1_out13, demultiplexer_2_out13);
  assign controlled_buffer_27_out = demultiplexer_2_out13 ? ValM : 64'bz;  // Controlled_Buffer controlled_buffer_28
  assign controlled_buffer_29_out = demultiplexer_1_out14 ? ValE : 64'bz;  // Controlled_Buffer controlled_buffer_29
  or or_15 (or_15_out, demultiplexer_1_out14, demultiplexer_2_out14);
  assign controlled_buffer_29_out = demultiplexer_2_out14 ? ValM : 64'bz;  // Controlled_Buffer controlled_buffer_30
  Register #(.width(64)) register_1 (
    .D(controlled_buffer_1_out), .en(or_1_out), .clk(Clk), .Q(register_1_q));  // open: clr
  Register #(.width(64)) register_2 (
    .D(controlled_buffer_3_out), .en(or_2_out), .clk(Clk), .Q(register_2_q));  // open: clr
  Register #(.width(64)) register_3 (
    .D(controlled_buffer_5_out), .en(or_3_out), .clk(Clk), .Q(register_3_q));  // open: clr
  Register #(.width(64)) register_4 (
    .D(controlled_buffer_7_out), .en(or_4_out), .clk(Clk), .Q(register_4_q));  // open: clr
  Register #(.width(64)) register_5 (
    .D(controlled_buffer_9_out), .en(or_5_out), .clk(Clk), .Q(register_5_q));  // open: clr
  Register #(.width(64)) register_6 (
    .D(controlled_buffer_11_out), .en(or_6_out), .clk(Clk), .Q(register_6_q));  // open: clr
  Register #(.width(64)) register_7 (
    .D(controlled_buffer_13_out), .en(or_7_out), .clk(Clk), .Q(register_7_q));  // open: clr
  Register #(.width(64)) register_8 (
    .D(controlled_buffer_15_out), .en(or_8_out), .clk(Clk), .Q(register_8_q));  // open: clr
  Register #(.width(64)) register_9 (
    .D(controlled_buffer_17_out), .en(or_9_out), .clk(Clk), .Q(register_9_q));  // open: clr
  Register #(.width(64)) register_10 (
    .D(controlled_buffer_19_out), .en(or_10_out), .clk(Clk), .Q(register_10_q));  // open: clr
  Register #(.width(64)) register_11 (
    .D(controlled_buffer_21_out), .en(or_11_out), .clk(Clk), .Q(register_11_q));  // open: clr
  Register #(.width(64)) register_12 (
    .D(controlled_buffer_23_out), .en(or_12_out), .clk(Clk), .Q(register_12_q));  // open: clr
  Register #(.width(64)) register_13 (
    .D(controlled_buffer_25_out), .en(or_13_out), .clk(Clk), .Q(register_13_q));  // open: clr
  Register #(.width(64)) register_14 (
    .D(controlled_buffer_27_out), .en(or_14_out), .clk(Clk), .Q(register_14_q));  // open: clr
  Register #(.width(64)) register_15 (
    .D(controlled_buffer_29_out), .en(or_15_out), .clk(Clk), .Q(register_15_q));  // open: clr
  Multiplexer #(.select(4), .width(64)) multiplexer_1 (
    .in0(register_1_q), .in1(register_2_q), .in2(register_3_q), .in3(register_4_q), .in4(register_5_q),
    .in5(register_6_q), .in6(register_7_q), .in7(register_8_q), .in8(register_9_q), .in9(register_10_q),
    .in10(register_11_q), .in11(register_12_q), .in12(register_13_q), .in13(register_14_q),
    .in14(register_15_q), .out(multiplexer_1_out), .sel(srcA));  // open: in15
  Multiplexer #(.select(4), .width(64)) multiplexer_2 (
    .in0(register_1_q), .in1(register_2_q), .in2(register_3_q), .in3(register_4_q), .in4(register_5_q),
    .in5(register_6_q), .in6(register_7_q), .in7(register_8_q), .in8(register_9_q), .in9(register_10_q),
    .in10(register_11_q), .in11(register_12_q), .in12(register_13_q), .in13(register_14_q),
    .in14(register_15_q), .out(multiplexer_2_out), .sel(srcB));  // open: in15
  Register #(.width(64)) register_16 (.D(multiplexer_1_out), .en(Read_Enable), .clk(Clk), .Q(ValA));  // open: clr
  Register #(.width(64)) register_17 (.D(multiplexer_2_out), .en(Read_Enable), .clk(Clk), .Q(ValB));  // open: clr

  // Notes on the sheet:
  //   rax
  //   rcx
  //   rdx
  //   rbx
  //   rsp
  //   rbp
  //   rsi
  //   rdi
  //   r8
  //   r9
  //   r10
  //   r11
  //   r12
  //   r13
  //   r14
endmodule

module Decode (
  input  [3:0] icode,
  input  [3:0] ifun,
  input  [63:0] ValM,
  input  [63:0] ValE,
  input  [3:0] rA,
  input  [3:0] rB,
  input  Read_Enable,
  input  Write_Enable,
  input  Clk,
  output [63:0] ValA,
  output [63:0] ValB
);

  wire and_1_out, and_2_out, decoder_1_out0, decoder_1_out1, decoder_1_out2, decoder_1_out3, decoder_1_out4,
       decoder_1_out5, decoder_1_out6, decoder_1_out7, decoder_1_out8, decoder_1_out9, decoder_1_out10,
       decoder_1_out11, dstE_Write_Enable_out, dstM_Write_Enable_out, or_1_out, or_2_out, or_3_out, or_4_out,
       rA_Read_Enable_out, rB_Read_Enable_out;
  wire [3:0] multiplexer_1_out, multiplexer_2_out, multiplexer_3_out, multiplexer_4_out, multiplexer_5_out,
       multiplexer_6_out, multiplexer_7_out;

  Decoder #(.select(4)) decoder_1 (
    .out0(decoder_1_out0), .out1(decoder_1_out1), .out2(decoder_1_out2), .out3(decoder_1_out3),
    .out4(decoder_1_out4), .out5(decoder_1_out5), .out6(decoder_1_out6), .out7(decoder_1_out7),
    .out8(decoder_1_out8), .out9(decoder_1_out9), .out10(decoder_1_out10), .out11(decoder_1_out11),
    .sel(icode));  // open: out12, out13, out14, out15, en
  or rA_Read_Enable (rA_Read_Enable_out, decoder_1_out2, decoder_1_out4, decoder_1_out6, decoder_1_out10, decoder_1_out11);
  Multiplexer #(.width(4)) multiplexer_1 (.in0(4'b1111), .in1(rA), .out(multiplexer_1_out), .sel(rA_Read_Enable_out));
  Multiplexer #(.width(4)) multiplexer_2 (
    .in0(multiplexer_1_out), .in1(4'b0100), .out(multiplexer_2_out), .sel(decoder_1_out11));
  or rB_Read_Enable (rB_Read_Enable_out, decoder_1_out11, decoder_1_out4, decoder_1_out5, decoder_1_out6, decoder_1_out10);
  Multiplexer #(.width(4)) multiplexer_3 (.in0(4'b1111), .in1(rB), .out(multiplexer_3_out), .sel(rB_Read_Enable_out));
  or or_1 (or_1_out, decoder_1_out11, decoder_1_out10);
  Multiplexer #(.width(4)) multiplexer_4 (
    .in0(multiplexer_3_out), .in1(4'b0100), .out(multiplexer_4_out), .sel(or_1_out));
  or dstE_Write_Enable (dstE_Write_Enable_out, decoder_1_out2, decoder_1_out3, decoder_1_out6, decoder_1_out8, decoder_1_out9, decoder_1_out10, decoder_1_out11);
  Multiplexer #(.width(4)) multiplexer_5 (
    .in0(4'b1111), .in1(rB), .out(multiplexer_5_out), .sel(dstE_Write_Enable_out));
  or or_2 (or_2_out, decoder_1_out8, decoder_1_out9, decoder_1_out10, decoder_1_out11);
  Multiplexer #(.width(4)) multiplexer_6 (
    .in0(multiplexer_5_out), .in1(4'b0100), .out(multiplexer_6_out), .sel(or_2_out));
  or dstM_Write_Enable (dstM_Write_Enable_out, decoder_1_out5, decoder_1_out11);
  or or_3 (or_3_out, dstM_Write_Enable_out, dstE_Write_Enable_out);
  Multiplexer #(.width(4)) multiplexer_7 (
    .in0(4'b1111), .in1(rA), .out(multiplexer_7_out), .sel(dstM_Write_Enable_out));
  or or_4 (or_4_out, rA_Read_Enable_out, rB_Read_Enable_out);
  and and_1 (and_1_out, or_4_out, Read_Enable);
  and and_2 (and_2_out, or_3_out, Write_Enable);
  Register_File register_file_1 (
    .srcA(multiplexer_2_out), .srcB(multiplexer_4_out), .dstE(multiplexer_6_out), .ValE(ValE),
    .dstM(multiplexer_7_out), .ValM(ValM), .Clk(Clk), .Read_Enable(and_1_out), .Write_Enable(and_2_out),
    .ValA(ValA), .ValB(ValB));

  // Notes on the sheet:
  //   2 clock ticks
endmodule
