// Logisim project Execute_Stage.circ as structural Verilog: 9 circuits, main circuit Execute
module Execute (
  input  [3:0] icode,
  input  [3:0] ifun,
  input  [63:0] valC,
  input  [63:0] valA,
  input  [63:0] valB,
  input  Clk,
  input  Enable,
  output Cnd,
  output [63:0] valE
);

  wire and_1_out, setcc_1_ccset;
  wire [1:0] alu_fun_1_op;
  wire [2:0] alu_1_cc, cc_1_cc_out;
  wire [63:0] alu_a_1_op1, alu_b_1_op2;

  cond cond_1 (.cc(cc_1_cc_out), .ifun(ifun), .Cnd(Cnd));
  CC cc_1 (.setCC(setcc_1_ccset), .ALU_Set(alu_1_cc), .Clk(and_1_out), .CC_out(cc_1_cc_out));
  SetCC setcc_1 (.icode(icode), .CCSet(setcc_1_ccset));
  ALU alu_1 (.op1(alu_a_1_op1), .op2(alu_b_1_op2), .ALU_fun(alu_fun_1_op), .CC(alu_1_cc), .valE(valE));
  ALU_A alu_a_1 (.valA(valA), .valC(valC), .icode(icode), .op1(alu_a_1_op1));
  ALU_B alu_b_1 (.valB(valB), .icode(icode), .op2(alu_b_1_op2));
  and and_1 (and_1_out, Clk, Enable);
  ALU_fun alu_fun_1 (.icode(icode), .ifun(ifun), .OP(alu_fun_1_op));

  // Notes on the sheet:
  //   1 clock tick
endmodule

module ALU_fun (
  input  [3:0] icode,
  input  [3:0] ifun,
  output [1:0] OP
);

  wire comparator_1_eq, comparator_2_eq, comparator_3_eq, comparator_4_eq, comparator_5_eq, comparator_6_eq;
  wire [3:0] multiplexer_1_out, multiplexer_2_out, multiplexer_3_out, multiplexer_4_out, multiplexer_6_out,
       multiplexer_7_out, multiplexer_8_out;
  wire [3:2] multiplexer_5_out;

  Comparator #(.width(4)) comparator_1 (.a(4'b0100), .b(icode), .eq(comparator_1_eq));  // open: gt, lt
  Multiplexer #(.width(4)) multiplexer_1 (.in1(4'b0000), .out(multiplexer_1_out), .sel(comparator_1_eq));  // open: in0
  Comparator #(.width(4)) comparator_2 (.a(4'b0101), .b(icode), .eq(comparator_2_eq));  // open: gt, lt
  Multiplexer #(.width(4)) multiplexer_2 (.in1(4'b0000), .out(multiplexer_2_out), .sel(comparator_2_eq));  // open: in0
  Comparator #(.width(4)) comparator_3 (.a(4'b0110), .b(icode), .eq(comparator_3_eq));  // open: gt, lt
  Multiplexer #(.select(4), .width(4)) multiplexer_3 (
    .in0(4'b0000), .in1(4'b0001), .in2(4'b0010), .in3(4'b0011), .out(multiplexer_3_out),
    .sel(multiplexer_4_out));  // open: in4, in5, in6, in7, in8, in9, in10, in11, in12, in13, in14, in15
  Multiplexer #(.width(4)) multiplexer_4 (.in1(ifun), .out(multiplexer_4_out), .sel(comparator_3_eq));  // open: in0
  Multiplexer #(.select(4), .width(4)) multiplexer_5 (
    .in4(multiplexer_1_out), .in5(multiplexer_2_out), .in6(multiplexer_3_out), .in8(multiplexer_6_out),
    .in10(multiplexer_7_out), .in11(multiplexer_8_out), .out({multiplexer_5_out, OP}), .sel(icode));  // open: in0, in1, in2, in3, in7, in9, in12, in13, in14, in15
  Comparator #(.width(4)) comparator_4 (.a(4'b1000), .b(icode), .eq(comparator_4_eq));  // open: gt, lt
  Multiplexer #(.width(4)) multiplexer_6 (.in1(4'b0001), .out(multiplexer_6_out), .sel(comparator_4_eq));  // open: in0
  Comparator #(.width(4)) comparator_5 (.a(4'b1010), .b(icode), .eq(comparator_5_eq));  // open: gt, lt
  Multiplexer #(.width(4)) multiplexer_7 (.in1(4'b0001), .out(multiplexer_7_out), .sel(comparator_5_eq));  // open: in0
  Comparator #(.width(4)) comparator_6 (.a(4'b1011), .b(icode), .eq(comparator_6_eq));  // open: gt, lt
  Multiplexer #(.width(4)) multiplexer_8 (.in1(4'b0000), .out(multiplexer_8_out), .sel(comparator_6_eq));  // open: in0
endmodule

module SetCC (
  input  [3:0] icode,
  output CCSet
);

  Comparator #(.width(4)) comparator_1 (.a(4'b0110), .b(icode), .eq(CCSet));  // open: gt, lt
endmodule

module ALU_A (
  input  [63:0] valA,
  input  [63:0] valC,
  input  [3:0] icode,
  output [63:0] op1
);

  Multiplexer #(.select(4), .width(64)) multiplexer_1 (
    .in2(valA), .in3(valC), .in4(valC), .in5(valC), .in6(valA), .in7(valC), .in8(64'h8), .in9(64'h8),
    .in10(64'h8), .in11(64'h8), .out(op1), .sel(icode));  // open: in0, in1, in12, in13, in14, in15
endmodule

module ALU_B (
  input  [63:0] valB,
  input  [3:0] icode,
  output [63:0] op2
);

  Multiplexer #(.select(4), .width(64)) multiplexer_1 (
    .in4(valB), .in5(valB), .in6(valB), .in8(valB), .in10(valB), .in11(valB), .out(op2), .sel(icode));  // open: in0, in1, in2, in3, in7, in9, in12, in13, in14, in15
endmodule

module CC (
  input  setCC,
  input  [2:0] ALU_Set,
  input  Clk,
  output [2:0] CC_out
);

  Register #(.width(3)) register_1 (.D(ALU_Set), .en(setCC), .clk(Clk), .Q(CC_out));  // open: clr
endmodule

module cond (
  input  [2:0] cc,
  input  [3:0] ifun,
  output Cnd
);

  wire and_1_out, not_1_out, not_2_out, not_3_out, not_4_out, or_1_out, xor_1_out, xor_2_out, xor_3_out,
       xor_4_out;

  or or_1 (or_1_out, cc[2], xor_1_out);
  xor xor_1 (xor_1_out, cc[1], cc[0]);
  xor xor_2 (xor_2_out, cc[1], cc[0]);
  not not_1 (not_1_out, cc[2]);
  xor xor_3 (xor_3_out, cc[1], cc[0]);
  not not_2 (not_2_out, xor_3_out);
  xor xor_4 (xor_4_out, cc[1], cc[0]);
  not not_3 (not_3_out, xor_4_out);
  not not_4 (not_4_out, cc[2]);
  and and_1 (and_1_out, not_3_out, not_4_out);
  Multiplexer #(.select(4)) multiplexer_1 (
    .in0(1'b1), .in1(or_1_out), .in2(xor_2_out), .in3(cc[2]), .in4(not_1_out), .in5(not_2_out),
    .in6(and_1_out), .out(Cnd), .sel(ifun));  // open: in7, in8, in9, in10, in11, in12, in13, in14, in15

  // Notes on the sheet:
  //   of, sf, zf
  //   jle
  //   jl
  //   je
  //   jne
  //   jge
  //   jg
  //   jmp
endmodule

module ALU (
  input  [63:0] op1,
  input  [63:0] op2,
  input  [1:0] ALU_fun,
  output [2:0] CC,
  output [63:0] valE
);

  wire comparator_1_eq, comparator_1_lt, comparator_2_eq, comparator_2_lt, comparator_3_eq, comparator_3_lt,
       comparator_4_eq, comparator_4_lt, gmsb_1_n, gmsb_2_n, gmsb_3_n, gmsb_4_n, gmsb_5_n, gmsb_6_n,
       not_1_out, not_2_out, xor_2_out, xor_3_out, xor_4_out, xor_5_out;
  wire [2:0] and_2_out, and_3_out;
  wire [2:1] multiplexer_6_out, multiplexer_8_out;
  wire [63:0] adder_1_out, and_1_out, subtractor_1_out, xor_1_out;

  Adder #(.width(64)) adder_1 (.a(op1), .b(op2), .out(adder_1_out));  // open: cin, cout
  assign and_1_out = op1 & op2;  // AND_Gate and_1, 64 bits wide
  assign xor_1_out = op1 ^ op2;  // XOR_Gate xor_1, 64 bits wide
  GMSB gmsb_1 (.i(op1), .n(gmsb_1_n));
  GMSB gmsb_2 (.i(op2), .n(gmsb_2_n));
  Subtractor #(.width(64)) subtractor_1 (.a(op2), .b(op1), .out(subtractor_1_out));  // open: bin, bout
  Comparator #(.width(64)) comparator_1 (
    .a(subtractor_1_out), .b({64{1'b0}}), .eq(comparator_1_eq), .lt(comparator_1_lt));  // open: gt
  GMSB gmsb_3 (.i(op2), .n(gmsb_3_n));
  GMSB gmsb_4 (.i(op1), .n(gmsb_4_n));
  Comparator #(.width(64)) comparator_2 (
    .a(adder_1_out), .b({64{1'b0}}), .eq(comparator_2_eq), .lt(comparator_2_lt));  // open: gt
  Comparator #(.width(64)) comparator_3 (
    .a(xor_1_out), .b({64{1'b0}}), .eq(comparator_3_eq), .lt(comparator_3_lt));  // open: gt
  GMSB gmsb_5 (.i(adder_1_out), .n(gmsb_5_n));
  xor xor_2 (xor_2_out, gmsb_1_n, gmsb_2_n);
  not not_1 (not_1_out, xor_2_out);
  GMSB gmsb_6 (.i(subtractor_1_out), .n(gmsb_6_n));
  xor xor_3 (xor_3_out, gmsb_3_n, gmsb_4_n);
  Comparator #(.width(64)) comparator_4 (
    .a(and_1_out), .b({64{1'b0}}), .eq(comparator_4_eq), .lt(comparator_4_lt));  // open: gt
  xor xor_4 (xor_4_out, gmsb_5_n, gmsb_1_n);
  xor xor_5 (xor_5_out, gmsb_6_n, gmsb_3_n);
  Multiplexer multiplexer_1 (.in0(1'b0), .in1(1'b1), .out(and_2_out[2]), .sel(comparator_2_eq));
  Multiplexer multiplexer_2 (.in0(1'b0), .in1(1'b1), .out(and_2_out[1]), .sel(comparator_2_lt));
  and and_2 (and_2_out[0], xor_4_out, not_1_out);
  Multiplexer multiplexer_3 (.in0(1'b0), .in1(1'b1), .out(and_3_out[2]), .sel(comparator_1_eq));
  Multiplexer multiplexer_4 (.in0(1'b0), .in1(1'b1), .out(and_3_out[1]), .sel(comparator_1_lt));
  not not_2 (not_2_out, xor_5_out);
  and and_3 (and_3_out[0], not_2_out, xor_3_out);
  Multiplexer multiplexer_5 (.in0(1'b0), .in1(1'b1), .out(multiplexer_6_out[2]), .sel(comparator_4_eq));
  Multiplexer multiplexer_6 (.in0(1'b0), .in1(1'b1), .out(multiplexer_6_out[1]), .sel(comparator_4_lt));
  Multiplexer multiplexer_7 (.in0(1'b0), .in1(1'b1), .out(multiplexer_8_out[2]), .sel(comparator_3_eq));
  Multiplexer multiplexer_8 (.in0(1'b0), .in1(1'b1), .out(multiplexer_8_out[1]), .sel(comparator_3_lt));
  Multiplexer #(.select(2), .width(64)) multiplexer_9 (
    .in0(adder_1_out), .in1(subtractor_1_out), .in2(and_1_out), .in3(xor_1_out), .out(valE), .sel(ALU_fun));
  Multiplexer #(.select(2), .width(3)) multiplexer_10 (
    .in0(and_2_out), .in1(and_3_out), .in2({multiplexer_6_out, 1'b0}), .in3({multiplexer_8_out, 1'b0}),
    .out(CC), .sel(ALU_fun));

  // Notes on the sheet:
  //   of, sf, zf
endmodule

module GMSB (
  input  [63:0] i,
  output n
);

  wire [63:0] shifter_1_out;

  Shifter #(.shift("lr"), .width(64)) shifter_1 (.in(i), .\dist ({6{1'b1}}), .out(shifter_1_out));
  BitSelector #(.width(64)) bitselector_1 (.in(shifter_1_out), .out(n), .sel({6{1'b0}}));
endmodule
