// Logisim project Fetch_Stage.circ as structural Verilog: 5 circuits, main circuit Fetch
module Fetch (
  input  [11:0] PC_in,
  input  Clk,
  input  Enable,
  output Halt,
  output [3:0] icode,
  output [3:0] ifun,
  output [3:0] rA,
  output [3:0] rB,
  output [63:0] ValC,
  output [11:0] Val_P
);

  wire and_1_out, and_2_out, and_3_out, comparator_1_eq, comparator_1_gt, comparator_1_lt, comparator_2_eq,
       decoder_1_out0, decoder_1_out1, decoder_1_out2, decoder_1_out3, decoder_1_out4, decoder_1_out5,
       decoder_1_out6, decoder_1_out7, decoder_1_out8, decoder_1_out9, decoder_1_out10, decoder_1_out11,
       Needs_Registers_out, Needs_ValC_out, or_1_out;
  wire [3:0] align_1_ra, align_1_rb, split_1_left, split_1_right;
  wire [7:0] counter_1_q, instruction_memory_1_byte0, instruction_memory_1_byte1, instruction_memory_1_byte2,
       instruction_memory_1_byte3, instruction_memory_1_byte4, instruction_memory_1_byte5,
       instruction_memory_1_byte6, instruction_memory_1_byte7, instruction_memory_1_byte8,
       instruction_memory_1_byte9;
  wire [11:0] pc_increment_1_pc_new;
  wire [63:0] align_1_valc;

  and and_1 (and_1_out, Clk, Enable);
  and and_2 (and_2_out, comparator_1_lt, and_1_out);
  Counter #(.max('ha)) counter_1 (.clk(and_1_out), .Q(counter_1_q));  // open: clr, load, up, count, D, carry
  Instruction_Memory instruction_memory_1 (
    .PC_in(PC_in), .clk(and_2_out), .Byte0(instruction_memory_1_byte0), .Byte1(instruction_memory_1_byte1),
    .Byte2(instruction_memory_1_byte2), .Byte3(instruction_memory_1_byte3),
    .Byte4(instruction_memory_1_byte4), .Byte5(instruction_memory_1_byte5),
    .Byte6(instruction_memory_1_byte6), .Byte7(instruction_memory_1_byte7),
    .Byte8(instruction_memory_1_byte8), .Byte9(instruction_memory_1_byte9));
  and and_3 (and_3_out, Enable, or_1_out);
  or or_1 (or_1_out, comparator_1_gt, comparator_1_eq);
  Comparator comparator_1 (.a(counter_1_q), .b(8'h9), .gt(comparator_1_gt), .eq(comparator_1_eq), .lt(comparator_1_lt));
  Split split_1 (.Byte0(instruction_memory_1_byte0), .left(split_1_left), .right(split_1_right));
  Align align_1 (
    .Needs_Register(Needs_Registers_out), .Byte0(instruction_memory_1_byte1),
    .Byte1(instruction_memory_1_byte2), .Byte2(instruction_memory_1_byte3),
    .Byte3(instruction_memory_1_byte4), .Byte4(instruction_memory_1_byte5),
    .Byte5(instruction_memory_1_byte6), .Byte6(instruction_memory_1_byte7),
    .Byte7(instruction_memory_1_byte8), .Byte8(instruction_memory_1_byte9), .rA(align_1_ra), .rB(align_1_rb),
    .ValC(align_1_valc));
  Decoder #(.select(4)) decoder_1 (
    .out0(decoder_1_out0), .out1(decoder_1_out1), .out2(decoder_1_out2), .out3(decoder_1_out3),
    .out4(decoder_1_out4), .out5(decoder_1_out5), .out6(decoder_1_out6), .out7(decoder_1_out7),
    .out8(decoder_1_out8), .out9(decoder_1_out9), .out10(decoder_1_out10), .out11(decoder_1_out11),
    .sel(split_1_left));  // open: out12, out13, out14, out15, en
  or Needs_Registers (Needs_Registers_out, decoder_1_out2, decoder_1_out3, decoder_1_out4, decoder_1_out5, decoder_1_out6, decoder_1_out10, decoder_1_out11);
  or Needs_ValC (Needs_ValC_out, decoder_1_out3, decoder_1_out4, decoder_1_out5, decoder_1_out7, decoder_1_out8);
  Comparator #(.width(4)) comparator_2 (.a(4'b0000), .b(icode), .eq(comparator_2_eq));  // open: gt, lt
  Register #(.width(4)) register_1 (.D(split_1_left), .en(and_3_out), .clk(and_1_out), .Q(icode));  // open: clr
  Register #(.width(4)) register_2 (.D(split_1_right), .en(and_3_out), .clk(and_1_out), .Q(ifun));  // open: clr
  Register #(.width(4)) register_3 (.D(align_1_ra), .en(and_3_out), .clk(and_1_out), .Q(rA));  // open: clr
  Register #(.width(4)) register_4 (.D(align_1_rb), .en(and_3_out), .clk(and_1_out), .Q(rB));  // open: clr
  PC_Increment pc_increment_1 (
    .PC_in(PC_in), .Needs_Registers(Needs_Registers_out), .Needs_ValC(Needs_ValC_out),
    .PC_new(pc_increment_1_pc_new));
  and and_4 (Halt, comparator_2_eq, comparator_1_gt);
  Register #(.width(64)) register_5 (.D(align_1_valc), .en(and_3_out), .clk(and_1_out), .Q(ValC));  // open: clr
  Register #(.width(12)) register_6 (
    .D(pc_increment_1_pc_new), .en(and_3_out), .clk(and_1_out), .Q(Val_P));  // open: clr

  // Notes on the sheet:
  //   Uses 10 clock cycles total
  //   Uses 10 Clock Cycles
endmodule

module Instruction_Memory (
  input  [11:0] PC_in,
  input  clk,
  output [7:0] Byte0,
  output [7:0] Byte1,
  output [7:0] Byte2,
  output [7:0] Byte3,
  output [7:0] Byte4,
  output [7:0] Byte5,
  output [7:0] Byte6,
  output [7:0] Byte7,
  output [7:0] Byte8,
  output [7:0] Byte9
);

  wire decoder_1_out0, decoder_1_out1, decoder_1_out2, decoder_1_out3, decoder_1_out4, decoder_1_out5,
       decoder_1_out6, decoder_1_out7, decoder_1_out8, decoder_1_out9;
  wire [3:0] bitselector_1_out;
  wire [7:0] demultiplexer_1_out0, demultiplexer_1_out1, demultiplexer_1_out2, demultiplexer_1_out3,
       demultiplexer_1_out4, demultiplexer_1_out5, demultiplexer_1_out6, demultiplexer_1_out7,
       demultiplexer_1_out8, demultiplexer_1_out9, rom_1_data;
  wire [11:0] adder_1_out, counter_1_q;

  Counter #(.max('h9), .width(12)) counter_1 (.clk(clk), .Q(counter_1_q));  // open: clr, load, up, count, D, carry
  Adder #(.width(12)) adder_1 (.a(PC_in), .b(counter_1_q), .out(adder_1_out));  // open: cin, cout
  ROM #(.addrWidth(12)) rom_1 (.addr(adder_1_out), .data(rom_1_data));
  BitSelector #(.group(4), .width(12)) bitselector_1 (.in(counter_1_q), .out(bitselector_1_out), .sel(2'b00));
  Decoder #(.select(4)) decoder_1 (
    .out0(decoder_1_out0), .out1(decoder_1_out1), .out2(decoder_1_out2), .out3(decoder_1_out3),
    .out4(decoder_1_out4), .out5(decoder_1_out5), .out6(decoder_1_out6), .out7(decoder_1_out7),
    .out8(decoder_1_out8), .out9(decoder_1_out9), .sel(bitselector_1_out));  // open: out10, out11, out12, out13, out14, out15, en
  Demultiplexer #(.select(4), .width(8)) demultiplexer_1 (
    .out0(demultiplexer_1_out0), .out1(demultiplexer_1_out1), .out2(demultiplexer_1_out2),
    .out3(demultiplexer_1_out3), .out4(demultiplexer_1_out4), .out5(demultiplexer_1_out5),
    .out6(demultiplexer_1_out6), .out7(demultiplexer_1_out7), .out8(demultiplexer_1_out8),
    .out9(demultiplexer_1_out9), .in(rom_1_data), .sel(bitselector_1_out));  // open: out10, out11, out12, out13, out14, out15
  Register register_1 (.D(demultiplexer_1_out0), .en(decoder_1_out0), .clk(clk), .Q(Byte0));  // open: clr
  Register register_2 (.D(demultiplexer_1_out1), .en(decoder_1_out1), .clk(clk), .Q(Byte1));  // open: clr
  Register register_3 (.D(demultiplexer_1_out2), .en(decoder_1_out2), .clk(clk), .Q(Byte2));  // open: clr
  Register register_4 (.D(demultiplexer_1_out3), .en(decoder_1_out3), .clk(clk), .Q(Byte3));  // open: clr
  Register register_5 (.D(demultiplexer_1_out4), .en(decoder_1_out4), .clk(clk), .Q(Byte4));  // open: clr
  Register register_6 (.D(demultiplexer_1_out5), .en(decoder_1_out5), .clk(clk), .Q(Byte5));  // open: clr
  Register register_7 (.D(demultiplexer_1_out6), .en(decoder_1_out6), .clk(clk), .Q(Byte6));  // open: clr
  Register register_8 (.D(demultiplexer_1_out7), .en(decoder_1_out7), .clk(clk), .Q(Byte7));  // open: clr
  Register register_9 (.D(demultiplexer_1_out8), .en(decoder_1_out8), .clk(clk), .Q(Byte8));  // open: clr
  Register register_10 (.D(demultiplexer_1_out9), .en(decoder_1_out9), .clk(clk), .Q(Byte9));  // open: clr

  // Notes on the sheet:
  //   contents of rom_1 (hex, n*v repeats v):
  //   fe ab cd
endmodule

module PC_Increment (
  input  [11:0] PC_in,
  input  Needs_Registers,
  input  Needs_ValC,
  output [11:0] PC_new
);

  wire [7:0] adder_1_out, bitselector_1_out, bitselector_2_out, shifter_1_out;
  wire [11:0] bitselector_3_out;

  BitSelector #(.group(8), .width(1)) bitselector_1 (.in(Needs_ValC), .out(bitselector_1_out), .sel(1'b0));
  Shifter shifter_1 (.in(bitselector_1_out), .\dist (3'b011), .out(shifter_1_out));
  BitSelector #(.group(8), .width(1)) bitselector_2 (.in(Needs_Registers), .out(bitselector_2_out), .sel(1'b0));
  BitSelector #(.group(12)) bitselector_3 (.in(adder_1_out), .out(bitselector_3_out), .sel(1'b0));
  Adder adder_1 (.a(bitselector_2_out), .b(shifter_1_out), .out(adder_1_out));  // open: cin, cout
  Adder #(.width(12)) adder_2 (.a(PC_in), .b(bitselector_3_out), .out(PC_new), .cin(1'b1));  // open: cout
endmodule

module Align (
  input  Needs_Register,
  input  [7:0] Byte0,
  input  [7:0] Byte1,
  input  [7:0] Byte2,
  input  [7:0] Byte3,
  input  [7:0] Byte4,
  input  [7:0] Byte5,
  input  [7:0] Byte6,
  input  [7:0] Byte7,
  input  [7:0] Byte8,
  output [3:0] rA,
  output [3:0] rB,
  output [63:0] ValC
);

  wire not_1_out;
  wire [5:0] multiplexer_1_out, multiplexer_2_out;
  wire [7:0] controlled_buffer_1_out;
  wire [63:0] bitselector_1_out, shifter_1_out, shifter_2_out;

  Shifter #(.shift("lr"), .width(64)) shifter_1 (
    .in({Byte7, Byte6, Byte5, Byte4, Byte3, Byte2, Byte1, Byte0}), .\dist (multiplexer_1_out),
    .out(shifter_1_out));
  Multiplexer #(.width(6)) multiplexer_1 (
    .in0({6{1'b0}}), .in1(6'b001000), .out(multiplexer_1_out), .sel(Needs_Register));
  not not_1 (not_1_out, Needs_Register);
  assign controlled_buffer_1_out = Needs_Register ? Byte8 : 8'bz;  // Controlled_Buffer controlled_buffer_1
  Multiplexer #(.width(6)) multiplexer_2 (
    .in0({6{1'b0}}), .in1(6'b111000), .out(multiplexer_2_out), .sel(Needs_Register));
  BitSelector #(.group(64)) bitselector_1 (.in(controlled_buffer_1_out), .out(bitselector_1_out), .sel(not_1_out));
  Shifter #(.width(64)) shifter_2 (.in(bitselector_1_out), .\dist (multiplexer_2_out), .out(shifter_2_out));
  Adder #(.width(64)) adder_1 (.a(shifter_1_out), .b(shifter_2_out), .out(ValC));  // open: cin, cout
  Split split_1 (.Byte0(Byte0), .left(rA), .right(rB));
endmodule

module Split (
  input  [7:0] Byte0,
  output [3:0] left,
  output [3:0] right
);

  wire [7:0] shifter_1_out;

  Shifter #(.shift("lr")) shifter_1 (.in(Byte0), .\dist (3'b100), .out(shifter_1_out));
  BitSelector #(.group(4)) bitselector_1 (.in(shifter_1_out), .out(left), .sel(1'b0));
  BitSelector #(.group(4)) bitselector_2 (.in(Byte0), .out(right), .sel(1'b0));
endmodule
