// Logisim project Memory_Stage.circ as structural Verilog: 2 circuits, main circuit Data_Memory
module Data_Memory (
  input  Read_Enable,
  input  Write_Enable,
  input  [63:0] Write_in,
  input  [11:0] PC_in,
  input  Reset,
  input  clk,
  output [7:0] Byte0,
  output [7:0] Byte1,
  output [7:0] Byte2,
  output [7:0] Byte3,
  output [7:0] Byte4,
  output [7:0] Byte5,
  output [7:0] Byte6,
  output [7:0] Byte7
);

  wire comparator_1_eq, decoder_1_out0, decoder_1_out1, decoder_1_out2, decoder_1_out3, decoder_1_out4,
       decoder_1_out5, decoder_1_out6, decoder_1_out7;
  wire [2:0] bitselector_1_out, subtractor_1_out;
  wire [3:0] bitselector_3_out, multiplexer_1_out, subtractor_2_out, subtractor_3_out;
  wire [7:0] bitselector_2_out, demultiplexer_1_out0, demultiplexer_1_out1, demultiplexer_1_out2,
       demultiplexer_1_out3, demultiplexer_1_out4, demultiplexer_1_out5, demultiplexer_1_out6,
       demultiplexer_1_out7, ram_1_dout;
  wire [11:0] adder_1_out, counter_1_q;

  Subtractor #(.width(3)) subtractor_1 (.a(3'b111), .b(bitselector_1_out), .out(subtractor_1_out));  // open: bin, bout
  Counter #(.max('h7), .width(12)) counter_1 (
    .clr(Reset), .clk(clk), .Q(counter_1_q));  // open: load, up, count, D, carry
  BitSelector #(.group(3), .width(12)) bitselector_1 (.in(counter_1_q), .out(bitselector_1_out), .sel(2'b00));
  BitSelector #(.group(8), .width(64)) bitselector_2 (.in(Write_in), .out(bitselector_2_out), .sel(subtractor_1_out));
  Adder #(.width(12)) adder_1 (.a(PC_in), .b(counter_1_q), .out(adder_1_out));  // open: cin, cout
  RAM #(.addrWidth(12)) ram_1 (
    .addr(adder_1_out), .we(Write_Enable), .oe(Read_Enable), .clk(clk), .din(bitselector_2_out),
    .dout(ram_1_dout));
  BitSelector #(.group(4), .width(12)) bitselector_3 (.in(counter_1_q), .out(bitselector_3_out), .sel(2'b00));
  Subtractor #(.width(4)) subtractor_2 (.a(bitselector_3_out), .b(4'b0001), .out(subtractor_2_out));  // open: bin, bout
  Comparator #(.width(4)) comparator_1 (.a(4'b0000), .b(bitselector_3_out), .eq(comparator_1_eq));  // open: gt, lt
  Multiplexer #(.width(4)) multiplexer_1 (
    .in0(subtractor_2_out), .in1(4'b0111), .out(multiplexer_1_out), .sel(comparator_1_eq));
  Decoder #(.select(4)) decoder_1 (
    .out0(decoder_1_out0), .out1(decoder_1_out1), .out2(decoder_1_out2), .out3(decoder_1_out3),
    .out4(decoder_1_out4), .out5(decoder_1_out5), .out6(decoder_1_out6), .out7(decoder_1_out7),
    .sel(subtractor_3_out));  // open: out8, out9, out10, out11, out12, out13, out14, out15, en
  Subtractor #(.width(4)) subtractor_3 (.a(4'b0111), .b(multiplexer_1_out), .out(subtractor_3_out));  // open: bin, bout
  Demultiplexer #(.select(4), .width(8)) demultiplexer_1 (
    .out0(demultiplexer_1_out0), .out1(demultiplexer_1_out1), .out2(demultiplexer_1_out2),
    .out3(demultiplexer_1_out3), .out4(demultiplexer_1_out4), .out5(demultiplexer_1_out5),
    .out6(demultiplexer_1_out6), .out7(demultiplexer_1_out7), .in(ram_1_dout), .sel(subtractor_3_out));  // open: out8, out9, out10, out11, out12, out13, out14, out15
  Register register_1 (.D(demultiplexer_1_out0), .en(decoder_1_out0), .clk(clk), .Q(Byte0));  // open: clr
  Register register_2 (.D(demultiplexer_1_out1), .en(decoder_1_out1), .clk(clk), .Q(Byte1));  // open: clr
  Register register_3 (.D(demultiplexer_1_out2), .en(decoder_1_out2), .clk(clk), .Q(Byte2));  // open: clr
  Register register_4 (.D(demultiplexer_1_out3), .en(decoder_1_out3), .clk(clk), .Q(Byte3));  // open: clr
  Register register_5 (.D(demultiplexer_1_out4), .en(decoder_1_out4), .clk(clk), .Q(Byte4));  // open: clr
  Register register_6 (.D(demultiplexer_1_out5), .en(decoder_1_out5), .clk(clk), .Q(Byte5));  // open: clr
  Register register_7 (.D(demultiplexer_1_out6), .en(decoder_1_out6), .clk(clk), .Q(Byte6));  // open: clr
  Register register_8 (.D(demultiplexer_1_out7), .en(decoder_1_out7), .clk(clk), .Q(Byte7));  // open: clr
endmodule

module Memory (
  input  [3:0] icode,
  input  [63:0] ValP,
  input  [63:0] ValE,
  input  [63:0] ValA,
  input  clk,
  input  Enable,
  output [63:0] ValM
);

  wire and_1_out, decoder_1_out4, decoder_1_out5, decoder_1_out8, decoder_1_out9, decoder_1_out10,
       decoder_1_out11, not_1_out, or_1_out, or_2_out, or_3_out, or_4_out;
  wire [11:0] bitselector_1_out;
  wire [63:0] multiplexer_1_out, multiplexer_2_out;

  Decoder #(.select(4)) decoder_1 (
    .out4(decoder_1_out4), .out5(decoder_1_out5), .out8(decoder_1_out8), .out9(decoder_1_out9),
    .out10(decoder_1_out10), .out11(decoder_1_out11), .sel(icode));  // open: out0, out1, out2, out3, out6, out7, out12, out13, out14, out15, en
  and and_1 (and_1_out, clk, Enable);
  not not_1 (not_1_out, Enable);
  or or_1 (or_1_out, decoder_1_out4, decoder_1_out10, decoder_1_out5, decoder_1_out9, decoder_1_out8);
  Multiplexer #(.width(64)) multiplexer_1 (.in0(ValA), .in1(ValE), .out(multiplexer_1_out), .sel(or_1_out));
  or or_2 (or_2_out, decoder_1_out4, decoder_1_out10);
  Multiplexer #(.width(64)) multiplexer_2 (.in0(ValP), .in1(ValA), .out(multiplexer_2_out), .sel(or_2_out));
  BitSelector #(.group(12), .width(64)) bitselector_1 (.in(multiplexer_1_out), .out(bitselector_1_out), .sel(3'b000));
  or or_3 (or_3_out, decoder_1_out4, decoder_1_out8, decoder_1_out10);
  or or_4 (or_4_out, decoder_1_out5, decoder_1_out9, decoder_1_out11);
  Data_Memory data_memory_1 (
    .Read_Enable(or_4_out), .Write_Enable(or_3_out), .Write_in(multiplexer_2_out), .PC_in(bitselector_1_out),
    .Reset(not_1_out), .clk(and_1_out), .Byte0(ValM[7:0]), .Byte1(ValM[15:8]), .Byte2(ValM[23:16]),
    .Byte3(ValM[31:24]), .Byte4(ValM[39:32]), .Byte5(ValM[47:40]), .Byte6(ValM[55:48]), .Byte7(ValM[63:56]));

  // Notes on the sheet:
  //   9 Clock ticks
endmodule
