// Logisim project PC_Update_Stage.circ as structural Verilog: 1 circuit, main circuit newPC
module newPC (
  input  [63:0] valP,
  input  [63:0] valC,
  input  Cnd,
  input  [63:0] valM,
  input  [3:0] icode,
  input  clk,
  input  Enable,
  output [11:0] new_PC
);

  wire [11:0] bitselector_1_out, bitselector_2_out, bitselector_3_out, multiplexer_1_out, multiplexer_2_out;

  BitSelector #(.group(12), .width(64)) bitselector_1 (.in(valM), .out(bitselector_1_out), .sel(3'b000));
  BitSelector #(.group(12), .width(64)) bitselector_2 (.in(valP), .out(bitselector_2_out), .sel(3'b000));
  BitSelector #(.group(12), .width(64)) bitselector_3 (.in(valC), .out(bitselector_3_out), .sel(3'b000));
  Multiplexer #(.width(12)) multiplexer_1 (
    .in0(bitselector_2_out), .in1(bitselector_3_out), .out(multiplexer_1_out), .sel(Cnd));
  Multiplexer #(.select(4), .width(12)) multiplexer_2 (
    .in0(bitselector_2_out), .in1(bitselector_2_out), .in2(bitselector_2_out), .in3(bitselector_2_out),
    .in4(bitselector_2_out), .in5(bitselector_2_out), .in6(bitselector_2_out), .in7(multiplexer_1_out),
    .in8(bitselector_1_out), .in9(bitselector_1_out), .in10(bitselector_2_out), .in11(bitselector_2_out),
    .in12(bitselector_2_out), .in13(bitselector_2_out), .in14(bitselector_2_out), .in15(bitselector_2_out),
    .out(multiplexer_2_out), .sel(icode));
  Register #(.width(12)) register_1 (.D(multiplexer_2_out), .en(Enable), .clk(clk), .Q(new_PC));  // open: clr
endmodule
